// Logisim project Autoampel-Sequenz.circ as structural Verilog: 1 circuit, main circuit main
module main (
);

  wire and_1_out, and_2_out, and_3_out, and_4_out, and_5_out, clock_1_out, counter_1_carry, counter_2_carry,
       counter_3_carry, counter_4_carry, d_ff_1_q, d_ff_2_q, d_ff_3_q, d_ff_4_q, d_ff_5_q, d_ff_6_q,
       not_1_out, not_2_out, not_3_out, or_1_out, or_2_out;

  Clock clock_1 (.out(clock_1_out));
  Button button_1 ();  // open: out
  and and_1 (and_1_out, clock_1_out, d_ff_3_q);
  and and_2 (and_2_out, clock_1_out, and_5_out);
  D_Flip_Flop d_ff_1 (.clk(clock_1_out), .D(clock_1_out), .Q(d_ff_1_q));  // open: Qn, preset, en, reset
  D_Flip_Flop d_ff_2 (
    .clk(counter_1_carry), .D(counter_1_carry), .Q(d_ff_2_q), .reset(d_ff_6_q));  // open: Qn, preset, en
  Counter #(.width(6), .max('h3f)) counter_1 (
    .carry(counter_1_carry), .clk(and_1_out));  // open: load, D, count, Q, clr
  D_Flip_Flop d_ff_3 (
    .clk(counter_2_carry), .D(counter_2_carry), .Q(d_ff_3_q), .reset(or_1_out));  // open: Qn, preset, en
  Counter #(.width(6), .max('h3f)) counter_2 (
    .carry(counter_2_carry), .clk(and_2_out));  // open: load, D, count, Q, clr
  not not_1 (not_1_out, d_ff_3_q);
  and and_3 (and_3_out, clock_1_out, d_ff_2_q);
  D_Flip_Flop d_ff_4 (.clk(d_ff_2_q), .D(d_ff_2_q), .Q(d_ff_4_q), .reset(not_1_out));  // open: Qn, preset, en
  or or_1 (or_1_out, d_ff_4_q, d_ff_6_q);
  Counter counter_3 (.carry(counter_3_carry), .clk(and_3_out));  // open: load, D, count, Q, clr
  D_Flip_Flop d_ff_5 (
    .clk(counter_3_carry), .D(counter_3_carry), .Q(d_ff_5_q), .reset(d_ff_6_q));  // open: Qn, preset, en
  or or_2 (or_2_out, d_ff_5_q, d_ff_3_q);
  and and_4 (and_4_out, clock_1_out, d_ff_5_q);
  not not_2 (not_2_out, or_2_out);
  not not_3 (not_3_out, d_ff_2_q);
  Counter #(.width(6), .max('h3f)) counter_4 (
    .carry(counter_4_carry), .clk(and_4_out));  // open: load, D, count, Q, clr
  D_Flip_Flop d_ff_6 (
    .clk(counter_4_carry), .D(counter_4_carry), .Q(d_ff_6_q), .reset(and_5_out));  // open: Qn, preset, en
  and and_5 (and_5_out, not_2_out, not_3_out, d_ff_1_q);
  LED led_1 (.in(d_ff_2_q));
  LED led_2 (.in(or_2_out));
  LED led_3 (.in(and_5_out));

  // Notes on the sheet:
  //   Rotschaltung
  //   Gelbschaltung
  //   Grünschaltung
  //   Rot-Gelbschaltung und Reset
endmodule
