// Logisim project Auto+Fußgänger+Taster.circ as structural Verilog: 1 circuit, main circuit main
module main (
);

  wire and_1_out, and_2_out, and_3_out, and_4_out, and_5_out, and_6_out, and_7_out, and_8_out, and_9_out,
       button_1_out, clock_1_out, counter_1_carry, counter_2_carry, counter_3_carry, counter_4_carry,
       counter_5_carry, counter_6_carry, counter_7_carry, d_ff_1_q, d_ff_2_q, d_ff_3_q, d_ff_4_q, d_ff_5_q,
       d_ff_6_q, d_ff_7_q, d_ff_8_q, not_1_out, not_2_out, not_3_out, not_4_out, not_5_out, not_6_out,
       or_1_out, or_2_out, or_3_out;

  Clock clock_1 (.out(clock_1_out));
  not not_1 (not_1_out, d_ff_1_q);
  Counter #(.width(2), .max('h3)) counter_1 (
    .carry(counter_1_carry), .clk(and_1_out), .clr(and_2_out));  // open: load, D, count, Q
  and and_1 (and_1_out, not_1_out, clock_1_out);
  Button button_1 (.out(button_1_out));
  and and_2 (and_2_out, clock_1_out, d_ff_1_q);
  and and_3 (and_3_out, or_1_out, d_ff_3_q);
  and and_4 (and_4_out, or_1_out, and_9_out);
  D_Flip_Flop d_ff_1 (.clk(button_1_out), .D(button_1_out), .Q(d_ff_1_q), .reset(d_ff_5_q));  // open: Qn, preset, en
  or or_1 (or_1_out, and_2_out, counter_1_carry);
  D_Flip_Flop d_ff_2 (
    .clk(counter_2_carry), .D(counter_2_carry), .Q(d_ff_2_q), .reset(d_ff_8_q));  // open: Qn, preset, en
  Counter #(.width(6), .max('h3f)) counter_2 (
    .carry(counter_2_carry), .clk(and_3_out));  // open: load, D, count, Q, clr
  D_Flip_Flop d_ff_3 (
    .clk(counter_3_carry), .D(counter_3_carry), .Q(d_ff_3_q), .reset(or_2_out));  // open: Qn, preset, en
  Counter #(.width(6), .max('h3f)) counter_3 (
    .carry(counter_3_carry), .clk(and_4_out));  // open: load, D, count, Q, clr
  not not_2 (not_2_out, d_ff_7_q);
  not not_3 (not_3_out, d_ff_3_q);
  D_Flip_Flop d_ff_4 (.clk(d_ff_2_q), .D(d_ff_2_q), .Q(d_ff_4_q), .reset(not_3_out));  // open: Qn, preset, en
  and and_5 (and_5_out, or_1_out, d_ff_2_q, not_2_out);
  or or_2 (or_2_out, d_ff_4_q, d_ff_8_q);
  Counter counter_4 (.carry(counter_4_carry), .clk(and_5_out));  // open: load, D, count, Q, clr
  D_Flip_Flop d_ff_5 (
    .clk(counter_4_carry), .D(counter_4_carry), .Q(d_ff_5_q), .reset(d_ff_7_q));  // open: Qn, preset, en
  Counter counter_5 (.carry(counter_5_carry), .clk(and_6_out));  // open: load, D, count, Q, clr
  and and_6 (and_6_out, or_1_out, d_ff_7_q);
  Counter counter_6 (.carry(counter_6_carry), .clk(and_7_out));  // open: load, D, count, Q, clr
  and and_7 (and_7_out, d_ff_5_q, or_1_out);
  D_Flip_Flop d_ff_6 (
    .clk(counter_5_carry), .D(counter_5_carry), .Q(d_ff_6_q), .reset(d_ff_8_q));  // open: Qn, preset, en
  or or_3 (or_3_out, d_ff_6_q, d_ff_3_q);
  D_Flip_Flop d_ff_7 (
    .clk(counter_6_carry), .D(counter_6_carry), .Q(d_ff_7_q), .reset(and_9_out));  // open: Qn, preset, en
  and and_8 (and_8_out, or_1_out, d_ff_6_q);
  not not_4 (not_4_out, d_ff_2_q);
  not not_5 (not_5_out, or_3_out);
  not not_6 (not_6_out, d_ff_5_q);
  Counter #(.width(6), .max('h3f)) counter_7 (
    .carry(counter_7_carry), .clk(and_8_out));  // open: load, D, count, Q, clr
  D_Flip_Flop d_ff_8 (
    .clk(counter_7_carry), .D(counter_7_carry), .Q(d_ff_8_q), .reset(and_9_out));  // open: Qn, preset, en
  and and_9 (and_9_out, not_5_out, not_4_out);
  LED led_1 (.in(not_6_out));
  LED led_2 (.in(not_6_out));
  LED led_3 (.in(d_ff_5_q));
  LED led_4 (.in(d_ff_2_q));
  LED led_5 (.in(or_3_out));
  LED led_6 (.in(and_9_out));

  // Notes on the sheet:
  //   Rotschaltung
  //   Gelbschaltung
  //   Grünschaltung
  //   Tastersystem beschleunigt den Takt
  //   Grün
  //   Rot-Gelbschaltung und Reset
  //   Allgemein Timing muss angepasst werden.
  //   Evtl.  Fehler prüfen und unnötiges entfernen
  //   Fußgängerampelsystem
endmodule
