// Logisim project Sortiert+Auto+Fußgänger+Taster.circ as structural Verilog: 6 circuits, main circuit main
module main (
);

  wire button_1_out, clock_1_out, \fußgängerampel_1_licht_signal ,
       \fußgängerampel_1_rot_gelb_start___takt_extra , G_R_G_out, gelbschaltung_1_gelb_signal_ro,
       minus_G__R_out, not_1_out, not_2_out, not_3_out, not_4_out, R_G_Reset_out,
       rot_gelb_schaltung_1_gelbsignal_or, rot_gelb_schaltung_1_rot_reset_und_gelb_or__reset,
       rotschaltung_1_gelb_reset, rotschaltung_1_rot_signal, taster_und_taktsystem_1_taktweiterleitungen;

  Clock clock_1 (.out(clock_1_out));
  Button button_1 (.out(button_1_out));
  Taster__und_Taktsystem taster_und_taktsystem_1 (
    .Takt(clock_1_out), .Taster(button_1_out),
    .Taktweiterleitungen(taster_und_taktsystem_1_taktweiterleitungen),
    .\Grün (\fußgängerampel_1_licht_signal ));
  Gelbschaltung gelbschaltung_1 (
    .Takt(taster_und_taktsystem_1_taktweiterleitungen), .\Grün (minus_G__R_out),
    .Rot(rotschaltung_1_rot_signal), .Final_Reset(R_G_Reset_out),
    .Gelb_Signal_Ro(gelbschaltung_1_gelb_signal_ro));
  Rotschaltung rotschaltung_1 (
    .Takt(taster_und_taktsystem_1_taktweiterleitungen), .Gelb_Ende(gelbschaltung_1_gelb_signal_ro),
    .Final_Reset(rot_gelb_schaltung_1_rot_reset_und_gelb_or__reset), .Invertiert_Gelb(not_1_out),
    .Rot_Signal(rotschaltung_1_rot_signal), .Gelb_Reset(rotschaltung_1_gelb_reset));
  not not_1 (not_1_out, gelbschaltung_1_gelb_signal_ro);
  Rot_Gelb_Schaltung rot_gelb_schaltung_1 (
    .Takt(taster_und_taktsystem_1_taktweiterleitungen),
    .F_Ampel_Sequenz_Ende(\fußgängerampel_1_rot_gelb_start___takt_extra ),
    .Rot_Reset_und_Gelb_OR__Reset(rot_gelb_schaltung_1_rot_reset_und_gelb_or__reset),
    .GelbSignal_OR(rot_gelb_schaltung_1_gelbsignal_or), .\Grün (minus_G__R_out));
  \Fußgängerampel  \fußgängerampel_1  (
    .Takt(taster_und_taktsystem_1_taktweiterleitungen), .Rot_einleitung(rotschaltung_1_rot_signal),
    .\Auto_Grün (minus_G__R_out),
    .Rot_Gelb_Start___Takt_extra(\fußgängerampel_1_rot_gelb_start___takt_extra ),
    .Licht_Signal(\fußgängerampel_1_licht_signal ));
  or R_G_Reset (R_G_Reset_out, rot_gelb_schaltung_1_rot_reset_und_gelb_or__reset, rotschaltung_1_gelb_reset);
  or G_R_G (G_R_G_out, rot_gelb_schaltung_1_gelbsignal_or, gelbschaltung_1_gelb_signal_ro);
  not not_2 (not_2_out, G_R_G_out);
  not not_3 (not_3_out, rotschaltung_1_rot_signal);
  not not_4 (not_4_out, \fußgängerampel_1_licht_signal );
  and minus_G__R (minus_G__R_out, not_2_out, not_3_out);
  LED led_1 (.in(not_4_out));
  LED led_2 (.in(not_4_out));
  LED led_3 (.in(\fußgängerampel_1_licht_signal ));
  LED led_4 (.in(rotschaltung_1_rot_signal));
  LED led_5 (.in(G_R_G_out));
  LED led_6 (.in(minus_G__R_out));

  // Notes on the sheet:
  //   Tastersystem beschleunigt den Takt
  //   Rot-Gelbschaltung und Reset
  //   Allgemein Timing muss angepasst werden.
  //   Fußgängerampelsystem
endmodule

// Rot
module Rotschaltung (
  input  Final_Reset,
  input  Takt,
  input  Gelb_Ende,
  input  Invertiert_Gelb,
  output Rot_Signal,
  output Gelb_Reset
);

  wire and_1_out, counter_1_carry;

  Counter #(.width(6), .max('h3f)) counter_1 (
    .carry(counter_1_carry), .clk(and_1_out));  // open: load, D, count, Q, clr
  and and_1 (and_1_out, Takt, Gelb_Ende);
  D_Flip_Flop d_ff_1 (
    .clk(counter_1_carry), .D(counter_1_carry), .Q(Rot_Signal), .reset(Final_Reset));  // open: Qn, preset, en
  D_Flip_Flop d_ff_2 (
    .clk(Rot_Signal), .D(Rot_Signal), .Q(Gelb_Reset), .reset(Invertiert_Gelb));  // open: Qn, preset, en

  // Notes on the sheet:
  //   Einleitung des roten Signal
  //   Reset des gelben Signals
endmodule

// Gelb
module Gelbschaltung (
  input  Rot,
  input  Final_Reset,
  input  Takt,
  input  \Grün ,
  output Gelb_Signal_Ro
);

  wire and_1_out, counter_1_carry, or_1_out;

  Counter #(.width(6), .max('h3f)) counter_1 (
    .carry(counter_1_carry), .clk(and_1_out));  // open: load, D, count, Q, clr
  and and_1 (and_1_out, Takt, \Grün );
  D_Flip_Flop d_ff_1 (
    .clk(counter_1_carry), .D(counter_1_carry), .Q(Gelb_Signal_Ro), .reset(or_1_out));  // open: Qn, preset, en
  or or_1 (or_1_out, Rot, Final_Reset);

  // Notes on the sheet:
  //   Einleitung des gelben Signals
  //   Reset des gelben Signals
endmodule

// F-Ampel
module \Fußgängerampel  (
  input  Rot_einleitung,
  input  Takt,
  input  \Auto_Grün ,
  output Rot_Gelb_Start___Takt_extra,
  output Licht_Signal
);

  wire and_1_out, and_2_out, counter_1_carry, counter_2_carry, not_1_out;

  not not_1 (not_1_out, Rot_Gelb_Start___Takt_extra);
  and and_1 (and_1_out, Takt, Rot_einleitung, not_1_out);
  Counter counter_1 (.carry(counter_1_carry), .clk(and_1_out));  // open: load, D, count, Q, clr
  D_Flip_Flop d_ff_1 (
    .clk(counter_1_carry), .D(counter_1_carry), .Q(Licht_Signal), .reset(Rot_Gelb_Start___Takt_extra));  // open: Qn, preset, en
  Counter counter_2 (.carry(counter_2_carry), .clk(and_2_out));  // open: load, D, count, Q, clr
  and and_2 (and_2_out, Licht_Signal, Takt);
  D_Flip_Flop d_ff_2 (
    .clk(counter_2_carry), .D(counter_2_carry), .Q(Rot_Gelb_Start___Takt_extra), .reset(\Auto_Grün ));  // open: Qn, preset, en

  // Notes on the sheet:
  //   Grün
  //   Einleitung des grünen F-Signals
  //   Reset des grünen F-Signals
endmodule

// Rot-Gelb + Reset
module Rot_Gelb_Schaltung (
  input  \Grün ,
  input  Takt,
  input  F_Ampel_Sequenz_Ende,
  output Rot_Reset_und_Gelb_OR__Reset,
  output GelbSignal_OR
);

  wire and_1_out, and_2_out, counter_1_carry, counter_2_carry;

  and and_1 (and_1_out, Takt, F_Ampel_Sequenz_Ende);
  Counter counter_1 (.carry(counter_1_carry), .clk(and_1_out));  // open: load, D, count, Q, clr
  D_Flip_Flop d_ff_1 (
    .clk(counter_1_carry), .D(counter_1_carry), .Q(GelbSignal_OR), .reset(Rot_Reset_und_Gelb_OR__Reset));  // open: Qn, preset, en
  and and_2 (and_2_out, Takt, GelbSignal_OR);
  Counter #(.width(6), .max('h3f)) counter_2 (
    .carry(counter_2_carry), .clk(and_2_out));  // open: load, D, count, Q, clr
  D_Flip_Flop d_ff_2 (
    .clk(counter_2_carry), .D(counter_2_carry), .Q(Rot_Reset_und_Gelb_OR__Reset), .reset(\Grün ));  // open: Qn, preset, en

  // Notes on the sheet:
  //   Einleitung des R/G-Signals
  //   Final Reset
endmodule

module Taster__und_Taktsystem (
  input  Takt,
  input  Taster,
  input  \Grün ,
  output Taktweiterleitungen
);

  wire and_1_out, and_2_out, counter_1_carry, d_ff_1_q, not_1_out;

  not not_1 (not_1_out, d_ff_1_q);
  D_Flip_Flop d_ff_1 (.clk(Taster), .D(Taster), .Q(d_ff_1_q), .reset(\Grün ));  // open: Qn, preset, en
  and and_1 (and_1_out, Takt, d_ff_1_q);
  and and_2 (and_2_out, Takt, not_1_out);
  Counter #(.width(2), .max('h3)) counter_1 (
    .carry(counter_1_carry), .clk(and_2_out), .clr(and_1_out));  // open: load, D, count, Q
  or or_1 (Taktweiterleitungen, counter_1_carry, and_1_out);
endmodule
